# Fritzing sketch breadboard (saved by Fritzing 0.9.4)
breadboards: 1

parts:
  LG3 = smd LED [color="Green (565nm)" package="1206 [SMD]"]
  LG2 = smd LED [color="Green (565nm)" package="1206 [SMD]"]
  LG1 = smd LED [color="Green (565nm)" package="1206 [SMD]"]
  LW = smd LED [color="White (4500K)" package="1206 [SMD]"]
  LR = smd LED [color="Red (660nm)" package="1206 [SMD]"]
  Part1 = Arduino Uno (Rev3) - ICSP
  R1 = Resistor [tolerance=±5% resistance=220 package="0805 [SMD]"]
  R2 = Resistor [tolerance=±5% resistance=220 package="0805 [SMD]"]
  R3 = Resistor [tolerance=±5% resistance=220 package="0805 [SMD]"]
  R4 = Resistor [tolerance=±5% resistance=220 package="0805 [SMD]"]
  R5 = Resistor [tolerance=±5% resistance=220 package="0805 [SMD]"]
  BTN1 = Momentary Switch [package=ksa_sealed_tac_switch]
  BTN2 = Momentary Switch [package=ksa_sealed_tac_switch]
  R6 = Resistor [tolerance=±5% resistance=10k package="2512 [SMD]"]
  R7 = Resistor [tolerance=±5% resistance=10k package="2512 [SMD]"]
  POT = POT [package=pot_alpha_rv16af-20]

nets:
  N1: LG3.cathode, LG2.cathode, LG1.cathode, LW.cathode, LR.cathode, Part1.GND, BTN1.1, BTN2.1, POT.E
  N2: LG3.anode, R1.Pin_0
  N3: LG2.anode, R2.Pin_0
  N4: LG1.anode, R3.Pin_0
  N5: LW.anode, R4.Pin_0
  N6: LR.anode, R5.Pin_0
  N7: Part1.A1, POT.S
  N8: Part1.D8, R3.Pin_1
  N9: Part1.D9_PWM, R4.Pin_1
  N10: Part1.D11_PWM/MOSI, R2.Pin_1
  N11: Part1.D12/MISO, R1.Pin_1
  N12: Part1.D2, BTN2.4
  N13: Part1.D3_PWM, BTN1.4
  N14: Part1.D7, R5.Pin_1
  N15: Part1.5V, R6.Pin_0, R7.Pin_0, POT.A
  N16: BTN1.3, R6.Pin_1
  N17: BTN2.3, R7.Pin_1
